// Digital circuit ALU.dig as structural Verilog
module ALU (
  input  [7:0] a,
  input  [2:0] op,
  input  s_i,
  input  [7:0] b,
  output [7:0] o,
  output s_o
);

  wire decoder_1_out_0, decoder_1_out_1, decoder_1_out_2, decoder_1_out_3, decoder_1_out_4, decoder_1_out_5,
       decoder_1_out_6, decoder_1_out_7;

  shifter_left Left (.i(a), .o(o), .si(s_i), .so(s_o), .e(decoder_1_out_0));
  shifter_right Right (.i(a), .o(o), .si(s_i), .so(s_o), .e(decoder_1_out_1));
  NOTer noter_1 (.i(a), .o(o), .e(decoder_1_out_2));
  ANDer ander_1 (.i(a), .i2(b), .o(o), .e(decoder_1_out_3));
  ORer orer_1 (.i(a), .i2(b), .o(o), .e(decoder_1_out_4));
  XORer xorer_1 (.i(a), .i2(b), .o(o), .e(decoder_1_out_5));
  LED led_1 (.in(decoder_1_out_7));
  LED led_2 (.in(decoder_1_out_6));
  Decoder #(.Selector_Bits(3)) decoder_1 (
    .sel(op), .out_0(decoder_1_out_0), .out_1(decoder_1_out_1), .out_2(decoder_1_out_2),
    .out_3(decoder_1_out_3), .out_4(decoder_1_out_4), .out_5(decoder_1_out_5), .out_6(decoder_1_out_6),
    .out_7(decoder_1_out_7));
endmodule
