// Digital circuit buffer_high_impedance.dig as structural Verilog
module buffer_high_impedance (
  input  i,
  input  e,
  output o
);

  wire nand_1_out, not_1_out, or_1_out;

  nand nand_1 (nand_1_out, i, e);
  not not_1 (not_1_out, e);
  PFET pfet_1 (.G(nand_1_out), .S(1'b1), .D(o));
  or or_1 (or_1_out, not_1_out, i);
  PFET pfet_2 (.G(or_1_out), .S(o), .D(1'b0));
endmodule
