// Digital circuit main.dig as structural Verilog
module main (
  input  in_1,
  input  in_2,
  input  in_3,
  input  in_4,
  input  in_5,
  input  in_6,
  input  in_7,
  input  in_8,
  input  in_9,
  input  in_10,
  input  in_11,
  input  in_12,
  input  in_16,
  input  in_17,
  input  [2:0] in_18,
  input  in_20,
  output [7:0] out_13,
  output [7:0] out_14,
  output [7:0] out_15,
  output out_19,
  output [7:0] out_21
);

  wire [7:0] alu_1_o;

  Temporary_register TMP (.o(out_21), .i(out_13), .s(in_12));
  ALU alu_1 (.a(out_13), .b(out_21), .o(alu_1_o), .op(in_18), .c_i(in_20), .c_o(out_19));
  ACC acc_1 (.o(out_13), .i(alu_1_o), .s(in_17), .e(in_16));
  registro R0 (.in(out_13), .out(out_13), .s(in_1), .e(in_2));
  registro R1 (.in(out_13), .out(out_13), .s(in_3), .e(in_4));
  registro R2 (.in(out_13), .out(out_13), .s(in_5), .e(in_6));
  registro R3 (.in(out_13), .out(out_13), .s(in_7), .e(in_8));
  MAR MAR (.out(out_14), .in(out_13), .s(in_9));
  RAM RAM (.a(out_14), .s(in_10), .e(in_11), .o(out_13), .i(out_13));

  assign out_15 = out_13;
endmodule
