// Digital circuit main_PC_clark.dig as structural Verilog
module main_PC_clark (
  input  i1,
  input  i2,
  output out_3
);

  wire nfet_1_d;

  NFET nfet_1 (.G(i1), .D(nfet_1_d), .S(out_3));
  NFET nfet_2 (.G(i2), .D(1'b0), .S(nfet_1_d));
  PullUp pullup_1 (.out(out_3));
endmodule
